// Logisim project 0 to 8 counter.circ as structural Verilog: 1 circuit, main circuit main
module main (
  input  in_1,
  input  in_2,
  output out_3,
  output out_4,
  output out_5,
  output out_6
);

  wire and_1_out, and_2_out, and_3_out, and_4_out, and_5_out, and_6_out, and_7_out, d_ff_1_q, d_ff_2_q,
       d_ff_3_q, d_ff_4_q, not_1_out, not_2_out, not_3_out, not_4_out, or_1_out, or_2_out;

  D_Flip_Flop d_ff_1 (.clk(in_1), .D(and_1_out), .Q(d_ff_1_q), .en(in_2));  // open: Qn, preset, reset
  not not_1 (not_1_out, d_ff_1_q);
  D_Flip_Flop d_ff_2 (.clk(in_1), .D(or_1_out), .Q(d_ff_2_q), .en(in_2));  // open: Qn, preset, reset
  not not_2 (not_2_out, d_ff_2_q);
  not not_3 (not_3_out, d_ff_3_q);
  and and_1 (and_1_out, not_4_out, not_1_out);
  and and_2 (and_2_out, not_2_out, d_ff_1_q, not_4_out);
  and and_3 (and_3_out, not_4_out, not_1_out, d_ff_2_q);
  and and_4 (and_4_out, not_4_out, d_ff_3_q, not_1_out);
  and and_5 (and_5_out, not_4_out, d_ff_3_q, not_2_out);
  and and_6 (and_6_out, not_4_out, not_3_out, d_ff_1_q, d_ff_2_q);
  and and_7 (and_7_out, d_ff_3_q, d_ff_2_q, d_ff_1_q, not_4_out);
  D_Flip_Flop d_ff_3 (.clk(in_1), .D(or_2_out), .Q(d_ff_3_q), .en(in_2));  // open: Qn, preset, reset
  or or_1 (or_1_out, and_2_out, and_3_out);
  or or_2 (or_2_out, and_4_out, and_5_out, and_6_out);
  D_Flip_Flop d_ff_4 (.clk(in_1), .D(and_7_out), .Q(d_ff_4_q), .en(in_2));  // open: Qn, preset, reset
  not not_4 (not_4_out, d_ff_4_q);
endmodule
