// Logisim project Bit wise AND.circ as structural Verilog: 1 circuit, main circuit main
module main (
  input  in_1,
  input  in_2,
  input  in_3,
  input  in_4,
  input  in_5,
  input  in_6,
  input  in_7,
  input  in_8,
  output out_9,
  output out_10,
  output out_11,
  output out_12
);

  and and_1 (out_9, in_7, in_8);
  and and_2 (out_10, in_5, in_6);
  and and_3 (out_11, in_3, in_4);
  and and_4 (out_12, in_1, in_2);
endmodule
