// Logisim project Gates using MUX.circ as structural Verilog: 1 circuit, main circuit main
module main (
  input  _0,
  input  A,
  input  A_2,
  input  _1,
  input  B,
  input  B_2,
  input  _1_2,
  input  _0_2,
  input  _1_3,
  input  _0_3,
  input  A_3,
  input  B_3,
  input  A_4,
  input  _1_4,
  input  _0_4,
  input  _0_5,
  input  A_5,
  input  B_4,
  output out_19,
  output out_20,
  output out_21,
  output out_22,
  output A_NOR_B
);

  wire multiplexer_1_out, multiplexer_5_out;

  Multiplexer #(.enable("false")) multiplexer_1 (.in0(_1_4), .in1(_0_4), .out(multiplexer_1_out), .sel(A_5));
  Multiplexer multiplexer_2 (.in0(_0), .in1(A_2), .out(out_19), .sel(B));  // open: en
  Multiplexer multiplexer_3 (.in0(_1_2), .in1(_0_2), .out(out_21), .sel(A_3));  // open: en
  Multiplexer #(.enable("false")) multiplexer_4 (.in0(multiplexer_1_out), .in1(_0_5), .out(A_NOR_B), .sel(B_4));
  Multiplexer multiplexer_5 (.in0(_1_3), .in1(_0_3), .out(multiplexer_5_out), .sel(B_3));  // open: en
  Multiplexer multiplexer_6 (.in0(A), .in1(_1), .out(out_20), .sel(B_2));  // open: en
  Multiplexer multiplexer_7 (.in0(B_3), .in1(multiplexer_5_out), .out(out_22), .sel(A_4));  // open: en

  // Notes on the sheet:
  //   A & B(AND)
  //   NOT
  //   A OR B
  //   A XOR B
endmodule
