// Logisim project Mux.circ as structural Verilog: 1 circuit, main circuit main
module main (
  input  [3:0] in_1,
  input  [3:0] in_2,
  input  [3:0] in_3,
  input  in_4,
  input  [1:0] in_5,
  output [3:0] out_6,
  output out_7
);

  wire [3:0] adder_1_out, and_1_out, not_1_out, xor_1_out;

  assign not_1_out = ~in_1;  // NOT_Gate not_1, 4 bits wide
  assign and_1_out = in_2 & in_3;  // AND_Gate and_1, 4 bits wide
  assign xor_1_out = in_2 ^ in_3;  // XOR_Gate xor_1, 4 bits wide
  Adder #(.width(4)) adder_1 (.a(in_2), .b(in_3), .out(adder_1_out), .cin(in_4), .cout(out_7));
  Multiplexer #(.select(2), .width(4), .enable("false")) multiplexer_1 (
    .in0(adder_1_out), .in1(xor_1_out), .in2(and_1_out), .in3(not_1_out), .out(out_6), .sel(in_5));
endmodule
