// Logisim project RAM.circ as structural Verilog: 14 circuits, main circuit main
module main (
  input  A,
  input  B,
  input  Cin,
  output Sum,
  output Cout
);

  wire and_1_out, and_2_out, and_3_out, xor_1_out;

  xor xor_1 (xor_1_out, A, B);
  and and_1 (and_1_out, A, B);
  and and_2 (and_2_out, A, Cin);
  and and_3 (and_3_out, B, Cin);
  xor xor_2 (Sum, xor_1_out, Cin);
  or or_1 (Cout, and_1_out, and_2_out, and_3_out);
endmodule

module _4bitRippleCarryAdder (
  input  cin,
  input  [3:0] input_1,
  input  [3:0] input2,
  output [3:0] out,
  output cout
);

  wire main_1_cout, main_2_cout, main_3_cout;

  main main_1 (.A(input_1[0]), .B(input2[0]), .Cin(cin), .Sum(out[0]), .Cout(main_1_cout));
  main main_2 (.A(input_1[1]), .B(input2[1]), .Cin(main_1_cout), .Sum(out[1]), .Cout(main_2_cout));
  main main_3 (.A(input_1[2]), .B(input2[2]), .Cin(main_2_cout), .Sum(out[2]), .Cout(main_3_cout));
  main main_4 (.A(input_1[3]), .B(input2[3]), .Cin(main_3_cout), .Sum(out[3]), .Cout(cout));
endmodule

module PCinSAP (
  input  in_1,
  input  in_2,
  output [3:0] out_3
);

  wire clock_1_out, j_k_ff_1_q, j_k_ff_1_qn, j_k_ff_2_q, j_k_ff_2_qn, j_k_ff_3_q, j_k_ff_3_qn, j_k_ff_4_q;

  Clock clock_1 (.out(clock_1_out));
  J_K_Flip_Flop j_k_ff_1 (
    .J(in_1), .clk(clock_1_out), .K(in_1), .Q(j_k_ff_1_q), .Qn(j_k_ff_1_qn));  // open: preset, en, reset
  J_K_Flip_Flop j_k_ff_2 (
    .J(in_1), .clk(j_k_ff_1_qn), .K(in_1), .Q(j_k_ff_2_q), .Qn(j_k_ff_2_qn));  // open: preset, en, reset
  J_K_Flip_Flop j_k_ff_3 (
    .J(in_1), .clk(j_k_ff_2_qn), .K(in_1), .Q(j_k_ff_3_q), .Qn(j_k_ff_3_qn));  // open: preset, en, reset
  J_K_Flip_Flop j_k_ff_4 (.J(in_1), .clk(j_k_ff_3_qn), .K(in_1), .Q(j_k_ff_4_q));  // open: Qn, preset, en, reset
  assign out_3[0] = in_2 ? j_k_ff_1_q : 1'bz;  // Controlled_Buffer controlled_buffer_1
  assign out_3[1] = in_2 ? j_k_ff_2_q : 1'bz;  // Controlled_Buffer controlled_buffer_2
  assign out_3[2] = in_2 ? j_k_ff_3_q : 1'bz;  // Controlled_Buffer controlled_buffer_3
  assign out_3[3] = in_2 ? j_k_ff_4_q : 1'bz;  // Controlled_Buffer controlled_buffer_4
endmodule

module PCinARM (
  input  in_1,
  output [15:0] out_2
);

  wire clock_1_out, not_1_out, not_2_out, not_3_out;

  Clock clock_1 (.out(clock_1_out));
  Counterfrom4 counterfrom4_1 (
    ._0(in_1), .clk(clock_1_out), .q0(out_2[0]), .q1(out_2[1]), .q2(out_2[2]), .out_6(out_2[3]));
  Counter counter_1 (.clk(not_3_out), .Q0(out_2[4]), .Q1(out_2[5]), .Q2(out_2[6]), .Q3(out_2[7]));
  Counter counter_2 (.clk(not_1_out), .Q0(out_2[8]), .Q1(out_2[9]), .Q2(out_2[10]), .Q3(out_2[11]));
  Counter counter_3 (.clk(not_2_out), .Q0(out_2[12]), .Q1(out_2[13]), .Q2(out_2[14]), .Q3(out_2[15]));
  not not_1 (not_1_out, out_2[7]);
  not not_2 (not_2_out, out_2[11]);
  not not_3 (not_3_out, out_2[3]);
endmodule

module Counter (
  input  clk,
  output Q0,
  output Q1,
  output Q2,
  output Q3
);

  wire j_k_ff_1_q, j_k_ff_1_qn, j_k_ff_2_q, j_k_ff_2_qn, j_k_ff_3_q, j_k_ff_3_qn, j_k_ff_4_q;

  J_K_Flip_Flop j_k_ff_1 (.J(1'b1), .clk(clk), .K(1'b1), .Q(j_k_ff_1_q), .Qn(j_k_ff_1_qn));  // open: preset, en, reset
  J_K_Flip_Flop j_k_ff_2 (
    .J(1'b1), .clk(j_k_ff_1_qn), .K(1'b1), .Q(j_k_ff_2_q), .Qn(j_k_ff_2_qn));  // open: preset, en, reset
  J_K_Flip_Flop j_k_ff_3 (
    .J(1'b1), .clk(j_k_ff_2_qn), .K(1'b1), .Q(j_k_ff_3_q), .Qn(j_k_ff_3_qn));  // open: preset, en, reset
  J_K_Flip_Flop j_k_ff_4 (.J(1'b1), .clk(j_k_ff_3_qn), .K(1'b1), .Q(j_k_ff_4_q));  // open: Qn, preset, en, reset
  assign Q0 = 1'b1 ? j_k_ff_1_q : 1'bz;  // Controlled_Buffer controlled_buffer_1
  assign Q1 = 1'b1 ? j_k_ff_2_q : 1'bz;  // Controlled_Buffer controlled_buffer_2
  assign Q2 = 1'b1 ? j_k_ff_3_q : 1'bz;  // Controlled_Buffer controlled_buffer_3
  assign Q3 = 1'b1 ? j_k_ff_4_q : 1'bz;  // Controlled_Buffer controlled_buffer_4
endmodule

module Counterfrom4 (
  input  _0,
  input  clk,
  output q0,
  output q1,
  output q2,
  output out_6
);

  wire j_k_ff_1_q, j_k_ff_2_q, j_k_ff_3_q, j_k_ff_3_qn, j_k_ff_4_q;

  J_K_Flip_Flop j_k_ff_1 (.J(_0), .clk(clk), .K(_0), .Q(j_k_ff_1_q));  // open: Qn, preset, en, reset
  J_K_Flip_Flop j_k_ff_2 (.J(_0), .clk(clk), .K(_0), .Q(j_k_ff_2_q));  // open: Qn, preset, en, reset
  J_K_Flip_Flop j_k_ff_3 (.J(1'b1), .clk(clk), .K(1'b1), .Q(j_k_ff_3_q), .Qn(j_k_ff_3_qn));  // open: preset, en, reset
  J_K_Flip_Flop j_k_ff_4 (.J(1'b1), .clk(j_k_ff_3_qn), .K(1'b1), .Q(j_k_ff_4_q));  // open: Qn, preset, en, reset
  assign q0 = 1'b1 ? j_k_ff_1_q : 1'bz;  // Controlled_Buffer controlled_buffer_1
  assign q1 = 1'b1 ? j_k_ff_2_q : 1'bz;  // Controlled_Buffer controlled_buffer_2
  assign q2 = 1'b1 ? j_k_ff_3_q : 1'bz;  // Controlled_Buffer controlled_buffer_3
  assign out_6 = 1'b1 ? j_k_ff_4_q : 1'bz;  // Controlled_Buffer controlled_buffer_4
endmodule

module mux (
  input  [3:0] I1,
  input  [3:0] I2,
  input  [3:0] I3,
  input  Enable,
  input  [1:0] select_lines,
  input  [3:0] I4,
  output [3:0] Output
);

  wire decoder_1_out0, decoder_1_out1, decoder_1_out2, decoder_1_out3;

  Decoder #(.select(2)) decoder_1 (
    .out0(decoder_1_out0), .out1(decoder_1_out1), .out2(decoder_1_out2), .out3(decoder_1_out3),
    .sel(select_lines), .en(Enable));
  assign Output = decoder_1_out0 ? I1 : 4'bz;  // Controlled_Buffer controlled_buffer_1
  assign Output = decoder_1_out1 ? I2 : 4'bz;  // Controlled_Buffer controlled_buffer_2
  assign Output = decoder_1_out2 ? I3 : 4'bz;  // Controlled_Buffer controlled_buffer_3
  assign Output = decoder_1_out3 ? I4 : 4'bz;  // Controlled_Buffer controlled_buffer_4
endmodule

module add_and_xor_comp (
  input  in_1,
  input  [3:0] in_2,
  input  [3:0] in_3,
  input  in_4,
  input  [1:0] in_5,
  output [3:0] out_6
);

  wire [3:0] and_1_out_3, comp_1_out_2, n4bitripplecarryadder_1_out, xor_1_out_3;

  _4bitRippleCarryAdder u_4bitripplecarryadder_1 (
    .cin(in_1), .input_1(in_2), .input2(in_3), .out(n4bitripplecarryadder_1_out));  // open: cout
  \and  and_1 (.in_1(in_2), .in_2(in_3), .out_3(and_1_out_3));
  \xor  xor_1 (.in_1(in_2), .in_2(in_3), .out_3(xor_1_out_3));
  comp comp_1 (.in_1(in_2), .out_2(comp_1_out_2));
  mux mux_1 (
    .I1(n4bitripplecarryadder_1_out), .I2(and_1_out_3), .I3(xor_1_out_3), .I4(comp_1_out_2), .Enable(in_4),
    .select_lines(in_5), .Output(out_6));
endmodule

module \and  (
  input  [3:0] in_1,
  input  [3:0] in_2,
  output [3:0] out_3
);

  assign out_3 = in_1 & in_2;  // AND_Gate and_1, 4 bits wide
endmodule

module \xor  (
  input  [3:0] in_1,
  input  [3:0] in_2,
  output [3:0] out_3
);

  assign out_3 = in_1 ^ in_2;  // XOR_Gate xor_1, 4 bits wide
endmodule

module comp (
  input  [3:0] in_1,
  output [3:0] out_2
);

  assign out_2 = ~in_1;  // NOT_Gate not_1, 4 bits wide
endmodule

module _2s_complement_adder_subtractor (
  input  [3:0] in_1,
  input  [3:0] in_2,
  input  in_3,
  output out_4,
  output [3:0] out_5
);

  wire main_1_cout, main_2_cout, main_3_cout, main_4_cout, xor_2_out, xor_3_out, xor_4_out, xor_5_out;

  xor xor_1 (out_4, main_2_cout, main_1_cout);
  xor xor_2 (xor_2_out, in_2[2], in_3);
  xor xor_3 (xor_3_out, in_2[3], in_3);
  main main_1 (.A(in_1[3]), .B(xor_3_out), .Cin(main_2_cout), .Sum(out_5[3]), .Cout(main_1_cout));
  xor xor_4 (xor_4_out, in_2[1], in_3);
  main main_2 (.A(in_1[2]), .B(xor_2_out), .Cin(main_3_cout), .Sum(out_5[2]), .Cout(main_2_cout));
  xor xor_5 (xor_5_out, in_2[0], in_3);
  main main_3 (.A(in_1[1]), .B(xor_4_out), .Cin(main_4_cout), .Sum(out_5[1]), .Cout(main_3_cout));
  main main_4 (.A(in_1[0]), .B(xor_5_out), .Cin(in_3), .Sum(out_5[0]), .Cout(main_4_cout));
endmodule

module ringcounter (
  input  in_1
);

  wire clock_1_out, d_ff_1_q, d_ff_2_q, d_ff_3_q, d_ff_4_q;

  Clock clock_1 (.out(clock_1_out));
  D_Flip_Flop #(.trigger("falling")) d_ff_1 (
    .clk(clock_1_out), .D(d_ff_4_q), .Q(d_ff_1_q), .preset(in_1));  // open: Qn, en, reset
  D_Flip_Flop #(.trigger("falling")) d_ff_2 (
    .clk(clock_1_out), .D(d_ff_1_q), .Q(d_ff_2_q));  // open: Qn, preset, en, reset
  D_Flip_Flop #(.trigger("falling")) d_ff_3 (
    .clk(clock_1_out), .D(d_ff_2_q), .Q(d_ff_3_q));  // open: Qn, preset, en, reset
  D_Flip_Flop #(.trigger("falling")) d_ff_4 (
    .clk(clock_1_out), .D(d_ff_3_q), .Q(d_ff_4_q));  // open: Qn, preset, en, reset
endmodule

module MAR_MDR_RAM (
  input  [2:0] in_1,
  input  [7:0] in_2,
  input  in_3,
  output [7:0] out_4
);

  wire clock_1_out, not_1_out;
  wire [2:0] register_1_q;
  wire [7:0] ram_1_data, register_2_q;

  Clock clock_1 (.out(clock_1_out));
  Register #(.width(3)) register_1 (.D(in_1), .Q(register_1_q), .clk(clock_1_out));  // open: en, clr
  Register register_2 (.D(in_2), .Q(register_2_q), .clk(clock_1_out));  // open: en, clr
  not not_1 (not_1_out, in_3);
  RAM #(.addrWidth(3), .bus("separate")) ram_1 (
    .addr(register_1_q), .din(register_2_q), .data(ram_1_data), .str(in_3), .clk(clock_1_out), .ld(not_1_out));  // open: sel, clr
  Register register_3 (.D(ram_1_data), .Q(out_4), .clk(clock_1_out));  // open: en, clr
endmodule
