// Logisim project Ring Counter.circ as structural Verilog: 1 circuit, main circuit main
module main (
  input  in_1,
  input  in_2,
  output [3:0] out_3
);

  wire clock_1_out, d_ff_4_qn;

  Clock clock_1 (.out(clock_1_out));
  D_Flip_Flop d_ff_1 (.clk(clock_1_out), .D(d_ff_4_qn), .Q(out_3[3]), .preset(in_1), .reset(in_2));  // open: Qn, en
  D_Flip_Flop d_ff_2 (.clk(clock_1_out), .D(out_3[3]), .Q(out_3[2]), .preset(in_1), .reset(in_2));  // open: Qn, en
  D_Flip_Flop d_ff_3 (.clk(clock_1_out), .D(out_3[2]), .Q(out_3[1]), .preset(in_1), .reset(in_2));  // open: Qn, en
  D_Flip_Flop d_ff_4 (
    .clk(clock_1_out), .D(out_3[1]), .Q(out_3[0]), .Qn(d_ff_4_qn), .preset(in_1), .reset(in_2));  // open: en
endmodule
