// Logisim project Ripply carry Adder.circ as structural Verilog: 1 circuit, main circuit main
module main (
  input  in_1,
  input  in_2,
  input  in_3,
  input  in_4,
  input  in_5,
  input  in_6,
  input  in_7,
  input  in_8,
  input  in_9,
  output out_10,
  output out_11,
  output out_12,
  output out_13,
  output out_14
);

  wire main_1_c, main_2_c, main_3_c;

  full_adder_main main_1 (.x(in_8), .y(in_6), .z(in_9), .S(out_10), .C(main_1_c));
  full_adder_main main_2 (.x(in_4), .y(in_1), .z(main_1_c), .S(out_11), .C(main_2_c));
  full_adder_main main_3 (.x(in_5), .y(in_2), .z(main_2_c), .S(out_12), .C(main_3_c));
  full_adder_main main_4 (.x(in_7), .y(in_3), .z(main_3_c), .S(out_13), .C(out_14));
endmodule
