// Logisim project endsem1.circ as structural Verilog: 1 circuit, main circuit main
// EXOR
module main (
  input  _0,
  input  _1,
  input  _1_2,
  input  [2:0] in_4,
  input  _0_2,
  input  [2:0] in_6,
  input  in_7,
  input  in_8,
  input  in_9,
  input  _0_3,
  input  _1_3,
  input  [2:0] in_12,
  output \output ,
  output output_2,
  output out_15,
  output output_3
);

  Multiplexer #(.select(3)) multiplexer_1 (
    .in0(_0), .in1(_1), .in2(_1), .in3(_0), .in4(_1), .in5(_0), .in6(_0), .in7(_1), .out(\output ), .sel(in_4));  // open: en
  nand nand_1 (out_15, in_7, in_8, in_9);
  Multiplexer #(.select(3)) multiplexer_2 (
    .in0(_1_2), .in1(_1_2), .in2(_1_2), .in3(_1_2), .in4(_1_2), .in5(_1_2), .in6(_1_2), .in7(_0_2),
    .out(output_2), .sel(in_6));  // open: en
  Multiplexer #(.select(3)) multiplexer_3 (
    .in0(_0_3), .in1(_0_3), .in2(_0_3), .in3(_1_3), .in4(_0_3), .in5(_1_3), .in6(_1_3), .in7(_1_3),
    .out(output_3), .sel(in_12));  // open: en
endmodule
