// Logisim project logisim.circ as structural Verilog
module half_adder (
  input  A,
  input  B,
  output SUM,
  output CARRY
);

  xor xor_1 (SUM, A, B);
  and and_1 (CARRY, B, A);
endmodule

module full_adder (
  input  A,
  input  B,
  input  cin,
  output SUM,
  output CARRY
);

  wire and_1_out, and_2_out, xor_1_out;

  xor xor_1 (xor_1_out, A, B);
  and and_1 (and_1_out, A, B);
  xor xor_2 (SUM, xor_1_out, cin);
  and and_2 (and_2_out, cin, xor_1_out);
  or or_1 (CARRY, and_2_out, and_1_out);
endmodule

module sap_program_counter (
  input  input_clock,
  output OUT
);

  wire d_ff_1_qn, d_ff_2_q, d_ff_2_qn, d_ff_3_q, d_ff_3_qn, d_ff_4_q, d_ff_4_qn;

  D_Flip_Flop #(.trigger("falling")) d_ff_1 (
    .clk(d_ff_2_q), .D(d_ff_1_qn), .Q(OUT), .Qn(d_ff_1_qn));  // open: preset, en, reset
  D_Flip_Flop #(.trigger("falling")) d_ff_2 (
    .clk(d_ff_3_q), .D(d_ff_2_qn), .Q(d_ff_2_q), .Qn(d_ff_2_qn));  // open: preset, en, reset
  D_Flip_Flop #(.trigger("falling")) d_ff_3 (
    .clk(d_ff_4_q), .D(d_ff_3_qn), .Q(d_ff_3_q), .Qn(d_ff_3_qn));  // open: preset, en, reset
  D_Flip_Flop #(.trigger("falling")) d_ff_4 (
    .clk(input_clock), .D(d_ff_4_qn), .Q(d_ff_4_q), .Qn(d_ff_4_qn));  // open: preset, en, reset
endmodule

module arm_program_counter (
  input  in_1,
  output final_output
);

  wire clock_1_out, d_ff_1_q, d_ff_1_qn, d_ff_2_q, d_ff_2_qn, d_ff_3_qn, d_ff_4_q, d_ff_4_qn,
       sap_program_counter_2_out, sap_program_counter_3_out, sap_program_counter_4_out,
       sap_program_counter_5_out, sap_program_counter_6_out, sap_program_counter_7_out;

  sap_program_counter sap_program_counter_1 (.input_clock(sap_program_counter_2_out), .OUT(final_output));
  sap_program_counter sap_program_counter_2 (.input_clock(sap_program_counter_3_out), .OUT(sap_program_counter_2_out));
  sap_program_counter sap_program_counter_3 (.input_clock(sap_program_counter_4_out), .OUT(sap_program_counter_3_out));
  sap_program_counter sap_program_counter_4 (.input_clock(sap_program_counter_5_out), .OUT(sap_program_counter_4_out));
  sap_program_counter sap_program_counter_5 (.input_clock(sap_program_counter_6_out), .OUT(sap_program_counter_5_out));
  sap_program_counter sap_program_counter_6 (.input_clock(sap_program_counter_7_out), .OUT(sap_program_counter_6_out));
  sap_program_counter sap_program_counter_7 (.input_clock(d_ff_1_q), .OUT(sap_program_counter_7_out));
  Clock clock_1 (.out(clock_1_out));
  D_Flip_Flop d_ff_1 (.clk(d_ff_2_q), .D(d_ff_1_qn), .Q(d_ff_1_q), .Qn(d_ff_1_qn));  // open: preset, en, reset
  D_Flip_Flop d_ff_2 (.clk(clock_1_out), .D(d_ff_2_qn), .Q(d_ff_2_q), .Qn(d_ff_2_qn));  // open: preset, en, reset
  D_Flip_Flop d_ff_3 (.clk(d_ff_4_q), .D(d_ff_3_qn), .Qn(d_ff_3_qn), .reset(in_1));  // open: Q, preset, en
  D_Flip_Flop d_ff_4 (.D(d_ff_4_qn), .Q(d_ff_4_q), .Qn(d_ff_4_qn), .reset(in_1));  // open: clk, preset, en
endmodule

module ripple_carry_adder (
  input  [3:0] A,
  input  [3:0] B,
  input  Cin,
  output final_cout,
  output S3,
  output S2,
  output S1,
  output S0
);

  wire full_adder_2_carry, full_adder_3_carry, full_adder_4_carry;

  full_adder full_adder_1 (.A(A[3]), .B(B[3]), .cin(full_adder_2_carry), .SUM(S3), .CARRY(final_cout));
  full_adder full_adder_2 (.A(A[2]), .B(B[2]), .cin(full_adder_3_carry), .SUM(S2), .CARRY(full_adder_2_carry));
  full_adder full_adder_3 (.A(A[1]), .B(B[1]), .cin(full_adder_4_carry), .SUM(S1), .CARRY(full_adder_3_carry));
  full_adder full_adder_4 (.A(A[0]), .B(B[0]), .cin(Cin), .SUM(S0), .CARRY(full_adder_4_carry));
endmodule

module ring_counter (
  output INSTRUCTION_6,
  output INSTRUCTION_5,
  output INSTRUCTION_4,
  output INSTRUCTION_3,
  output INSTRUCTION_2,
  output INSTRUCTION
);

  wire clock_1_out, d_ff_1_q, d_ff_1_qn, d_ff_2_q, d_ff_2_qn, d_ff_3_q, d_ff_3_qn, not_1_out;

  D_Flip_Flop #(.trigger("falling")) d_ff_1 (
    .clk(d_ff_2_q), .D(d_ff_1_qn), .Q(d_ff_1_q), .Qn(d_ff_1_qn));  // open: preset, en, reset
  D_Flip_Flop #(.trigger("falling")) d_ff_2 (
    .clk(d_ff_3_q), .D(d_ff_2_qn), .Q(d_ff_2_q), .Qn(d_ff_2_qn));  // open: preset, en, reset
  Clock clock_1 (.out(clock_1_out));
  D_Flip_Flop #(.trigger("falling")) d_ff_3 (
    .clk(clock_1_out), .D(d_ff_3_qn), .Q(d_ff_3_q), .Qn(d_ff_3_qn));  // open: preset, en, reset
  and and_1 (INSTRUCTION_6, d_ff_1_q, ~d_ff_2_q, d_ff_3_q);  // AND_Gate
  and and_2 (INSTRUCTION_5, d_ff_1_q, ~d_ff_2_q, ~d_ff_3_q);  // AND_Gate
  and and_3 (INSTRUCTION_4, ~d_ff_1_q, d_ff_2_q, d_ff_3_q);  // AND_Gate
  and and_4 (INSTRUCTION_3, ~d_ff_1_q, d_ff_2_q, ~d_ff_3_q);  // AND_Gate
  and and_5 (INSTRUCTION_2, ~d_ff_1_q, ~d_ff_2_q, d_ff_3_q);  // AND_Gate
  and and_6 (INSTRUCTION, ~d_ff_1_q, ~d_ff_2_q, ~d_ff_3_q);  // AND_Gate
  not not_1 (not_1_out, INSTRUCTION_6);
endmodule

module barrel_shifter (
  input  in_1,
  input  in_2,
  input  in_3,
  input  in_4,
  input  [1:0] in_5,
  output out_6,
  output out_7,
  output out_8,
  output out_9
);

  wire decoder_1_out0, decoder_1_out1, decoder_1_out2, decoder_1_out3;

  Decoder #(.select(2)) decoder_1 (
    .out0(decoder_1_out0), .out1(decoder_1_out1), .out2(decoder_1_out2), .out3(decoder_1_out3), .sel(in_5));  // open: en
  assign out_6 = decoder_1_out3 ? in_1 : 1'bz;  // Controlled_Buffer controlled_buffer_1
  assign out_7 = decoder_1_out2 ? in_1 : 1'bz;  // Controlled_Buffer controlled_buffer_2
  assign out_8 = decoder_1_out1 ? in_1 : 1'bz;  // Controlled_Buffer controlled_buffer_3
  assign out_9 = decoder_1_out0 ? in_1 : 1'bz;  // Controlled_Buffer controlled_buffer_4
  assign out_6 = decoder_1_out2 ? in_2 : 1'bz;  // Controlled_Buffer controlled_buffer_5
  assign out_7 = decoder_1_out1 ? in_2 : 1'bz;  // Controlled_Buffer controlled_buffer_6
  assign out_8 = decoder_1_out0 ? in_2 : 1'bz;  // Controlled_Buffer controlled_buffer_7
  assign out_9 = decoder_1_out3 ? in_2 : 1'bz;  // Controlled_Buffer controlled_buffer_8
  assign out_6 = decoder_1_out1 ? in_3 : 1'bz;  // Controlled_Buffer controlled_buffer_9
  assign out_7 = decoder_1_out0 ? in_3 : 1'bz;  // Controlled_Buffer controlled_buffer_10
  assign out_8 = decoder_1_out3 ? in_3 : 1'bz;  // Controlled_Buffer controlled_buffer_11
  assign out_9 = decoder_1_out2 ? in_3 : 1'bz;  // Controlled_Buffer controlled_buffer_12
  assign out_6 = decoder_1_out0 ? in_4 : 1'bz;  // Controlled_Buffer controlled_buffer_13
  assign out_7 = decoder_1_out3 ? in_4 : 1'bz;  // Controlled_Buffer controlled_buffer_14
  assign out_8 = decoder_1_out2 ? in_4 : 1'bz;  // Controlled_Buffer controlled_buffer_15
  assign out_9 = decoder_1_out1 ? in_4 : 1'bz;  // Controlled_Buffer controlled_buffer_16
endmodule

module register_file (
);

  wire [7:0] ram_1_data, undriven;

  RAM #(.bus("separate")) ram_1 (.addr(undriven), .data(ram_1_data));  // open: din, str, sel, clk, ld, clr
endmodule
