// Logisim project mux_internal.circ as structural Verilog: 1 circuit, main circuit main
module main (
  input  in_1,
  input  in_2,
  input  in_3,
  input  in_4,
  input  in_5,
  input  in_6,
  input  in_7,
  input  in_8
);

  wire and_1_out, and_2_out, and_3_out, and_4_out, controlled_buffer_1_out, not_1_out, not_2_out, or_1_out;

  not not_1 (not_1_out, in_6);
  not not_2 (not_2_out, in_8);
  and and_1 (and_1_out, in_1, not_1_out, not_2_out);
  and and_2 (and_2_out, in_2, not_1_out, in_8);
  and and_3 (and_3_out, in_4, in_6, not_2_out);
  and and_4 (and_4_out, in_6, in_6, in_8);
  or or_1 (or_1_out, and_1_out, and_2_out, and_3_out, and_4_out);
  assign controlled_buffer_1_out = in_5 ? or_1_out : 1'bz;  // Controlled_Buffer controlled_buffer_1

  assign in_7 = in_6;
endmodule
