// Logisim project pc for arm.circ as structural Verilog: 1 circuit, main circuit main
module main (
  input  in_1,
  input  in_2,
  input  in_3,
  output out_4,
  output out_5,
  output out_6,
  output out_7,
  output out_8,
  output out_9,
  output out_10,
  output out_11,
  output out_12,
  output out_13,
  output out_14,
  output out_15,
  output out_16,
  output out_17,
  output out_18,
  output out_19
);

  wire clock_1_out, j_k_ff_1_q, j_k_ff_2_q, j_k_ff_3_q, j_k_ff_4_q, j_k_ff_5_q, j_k_ff_6_q, j_k_ff_7_q,
       j_k_ff_8_q, j_k_ff_9_q, j_k_ff_10_q, j_k_ff_11_q, j_k_ff_12_q, j_k_ff_13_q, j_k_ff_14_q, j_k_ff_15_q,
       j_k_ff_16_q;

  Clock clock_1 (.out(clock_1_out));
  J_K_Flip_Flop j_k_ff_1 (.J(in_1), .clk(clock_1_out), .K(in_1), .Q(j_k_ff_1_q), .reset(in_2));  // open: Qn, preset, en
  assign out_4 = in_3 ? ~j_k_ff_1_q : 1'bz;  // Controlled_Inverter controlled_inverter_1
  J_K_Flip_Flop j_k_ff_2 (.J(in_1), .clk(j_k_ff_1_q), .K(in_1), .Q(j_k_ff_2_q), .reset(in_2));  // open: Qn, preset, en
  assign out_5 = in_3 ? ~j_k_ff_2_q : 1'bz;  // Controlled_Inverter controlled_inverter_2
  J_K_Flip_Flop j_k_ff_3 (.J(in_1), .clk(j_k_ff_2_q), .K(in_1), .Q(j_k_ff_3_q), .reset(in_2));  // open: Qn, preset, en
  assign out_6 = in_3 ? ~j_k_ff_3_q : 1'bz;  // Controlled_Inverter controlled_inverter_3
  J_K_Flip_Flop j_k_ff_4 (.J(in_1), .clk(j_k_ff_3_q), .K(in_1), .Q(j_k_ff_4_q), .reset(in_2));  // open: Qn, preset, en
  assign out_7 = in_3 ? ~j_k_ff_4_q : 1'bz;  // Controlled_Inverter controlled_inverter_4
  J_K_Flip_Flop j_k_ff_5 (.J(in_1), .clk(j_k_ff_4_q), .K(in_1), .Q(j_k_ff_5_q), .reset(in_2));  // open: Qn, preset, en
  assign out_8 = in_3 ? ~j_k_ff_5_q : 1'bz;  // Controlled_Inverter controlled_inverter_5
  J_K_Flip_Flop j_k_ff_6 (.J(in_1), .clk(j_k_ff_5_q), .K(in_1), .Q(j_k_ff_6_q), .reset(in_2));  // open: Qn, preset, en
  assign out_9 = in_3 ? ~j_k_ff_6_q : 1'bz;  // Controlled_Inverter controlled_inverter_6
  J_K_Flip_Flop j_k_ff_7 (.J(in_1), .clk(j_k_ff_6_q), .K(in_1), .Q(j_k_ff_7_q), .reset(in_2));  // open: Qn, preset, en
  assign out_10 = in_3 ? ~j_k_ff_7_q : 1'bz;  // Controlled_Inverter controlled_inverter_7
  J_K_Flip_Flop j_k_ff_8 (.J(in_1), .clk(j_k_ff_7_q), .K(in_1), .Q(j_k_ff_8_q), .reset(in_2));  // open: Qn, preset, en
  assign out_11 = in_3 ? ~j_k_ff_8_q : 1'bz;  // Controlled_Inverter controlled_inverter_8
  J_K_Flip_Flop j_k_ff_9 (.J(in_1), .clk(j_k_ff_8_q), .K(in_1), .Q(j_k_ff_9_q), .reset(in_2));  // open: Qn, preset, en
  assign out_12 = in_3 ? ~j_k_ff_9_q : 1'bz;  // Controlled_Inverter controlled_inverter_9
  J_K_Flip_Flop j_k_ff_10 (
    .J(in_1), .clk(j_k_ff_9_q), .K(in_1), .Q(j_k_ff_10_q), .reset(in_2));  // open: Qn, preset, en
  assign out_13 = in_3 ? ~j_k_ff_10_q : 1'bz;  // Controlled_Inverter controlled_inverter_10
  J_K_Flip_Flop j_k_ff_11 (
    .J(in_1), .clk(j_k_ff_10_q), .K(in_1), .Q(j_k_ff_11_q), .reset(in_2));  // open: Qn, preset, en
  assign out_14 = in_3 ? ~j_k_ff_11_q : 1'bz;  // Controlled_Inverter controlled_inverter_11
  J_K_Flip_Flop j_k_ff_12 (
    .J(in_1), .clk(j_k_ff_11_q), .K(in_1), .Q(j_k_ff_12_q), .reset(in_2));  // open: Qn, preset, en
  assign out_15 = in_3 ? ~j_k_ff_12_q : 1'bz;  // Controlled_Inverter controlled_inverter_12
  J_K_Flip_Flop j_k_ff_13 (
    .J(in_1), .clk(j_k_ff_12_q), .K(in_1), .Q(j_k_ff_13_q), .reset(in_2));  // open: Qn, preset, en
  assign out_16 = in_3 ? ~j_k_ff_13_q : 1'bz;  // Controlled_Inverter controlled_inverter_13
  J_K_Flip_Flop j_k_ff_14 (
    .J(in_1), .clk(j_k_ff_13_q), .K(in_1), .Q(j_k_ff_14_q), .reset(in_2));  // open: Qn, preset, en
  assign out_17 = in_3 ? ~j_k_ff_14_q : 1'bz;  // Controlled_Inverter controlled_inverter_14
  J_K_Flip_Flop j_k_ff_15 (
    .J(in_1), .clk(j_k_ff_14_q), .K(in_1), .Q(j_k_ff_15_q), .reset(in_2));  // open: Qn, preset, en
  assign out_18 = in_3 ? ~j_k_ff_15_q : 1'bz;  // Controlled_Inverter controlled_inverter_15
  J_K_Flip_Flop j_k_ff_16 (
    .J(in_1), .clk(j_k_ff_15_q), .K(in_1), .Q(j_k_ff_16_q), .reset(in_2));  // open: Qn, preset, en
  assign out_19 = in_3 ? ~j_k_ff_16_q : 1'bz;  // Controlled_Inverter controlled_inverter_16
endmodule
