// Logisim project pc for sap.circ as structural Verilog: 1 circuit, main circuit main
module main (
  input  Cp,
  input  CLR,
  input  Ep,
  output out_4,
  output out_5,
  output out_6,
  output out_7
);

  wire CLK_out, j_k_ff_1_q, j_k_ff_2_q, j_k_ff_3_q, j_k_ff_4_q;

  Clock CLK (.out(CLK_out));
  J_K_Flip_Flop j_k_ff_1 (.J(Cp), .clk(CLK_out), .K(Cp), .Q(j_k_ff_1_q), .reset(CLR));  // open: Qn, preset, en
  assign out_4 = Ep ? ~j_k_ff_1_q : 1'bz;  // Controlled_Inverter controlled_inverter_1
  J_K_Flip_Flop j_k_ff_2 (.J(Cp), .clk(j_k_ff_1_q), .K(Cp), .Q(j_k_ff_2_q), .reset(CLR));  // open: Qn, preset, en
  assign out_5 = Ep ? ~j_k_ff_2_q : 1'bz;  // Controlled_Inverter controlled_inverter_2
  J_K_Flip_Flop j_k_ff_3 (.J(Cp), .clk(j_k_ff_2_q), .K(Cp), .Q(j_k_ff_3_q), .reset(CLR));  // open: Qn, preset, en
  assign out_6 = Ep ? ~j_k_ff_3_q : 1'bz;  // Controlled_Inverter controlled_inverter_3
  J_K_Flip_Flop j_k_ff_4 (.J(Cp), .clk(j_k_ff_3_q), .K(Cp), .Q(j_k_ff_4_q), .reset(CLR));  // open: Qn, preset, en
  assign out_7 = Ep ? ~j_k_ff_4_q : 1'bz;  // Controlled_Inverter controlled_inverter_4
endmodule
