// Logisim project register2.circ as structural Verilog: 1 circuit, main circuit main
module main (
  input  Load,
  input  [2:0] in_2,
  input  [2:0] in_3,
  input  [2:0] in_4,
  input  [7:0] Data,
  input  in_6,
  output [7:0] out_7,
  output [7:0] out_8
);

  wire and_1_out, and_2_out, and_3_out, and_4_out, and_5_out, and_6_out, and_7_out, and_8_out, clock_out,
       decoder_1_out0, decoder_1_out1, decoder_1_out2, decoder_1_out3, decoder_1_out4, decoder_1_out5,
       decoder_1_out6, decoder_1_out7;
  wire [7:0] multiplexer_1_out, register_1_q, register_2_q, register_3_q, register_4_q, register_5_q,
       register_6_q, register_7_q, register_8_q;

  Decoder #(.select(3), .enable("false")) decoder_1 (
    .out0(decoder_1_out0), .out1(decoder_1_out1), .out2(decoder_1_out2), .out3(decoder_1_out3),
    .out4(decoder_1_out4), .out5(decoder_1_out5), .out6(decoder_1_out6), .out7(decoder_1_out7), .sel(in_3));
  Multiplexer #(.width(8), .enable("false")) multiplexer_1 (
    .in0(Data), .in1(out_8), .out(multiplexer_1_out), .sel(in_6));
  and and_1 (and_1_out, Load, decoder_1_out0);
  and and_2 (and_2_out, Load, decoder_1_out1);
  and and_3 (and_3_out, Load, decoder_1_out2);
  and and_4 (and_4_out, Load, decoder_1_out3);
  and and_5 (and_5_out, Load, decoder_1_out4);
  and and_6 (and_6_out, Load, decoder_1_out5);
  and and_7 (and_7_out, Load, decoder_1_out6);
  and and_8 (and_8_out, Load, decoder_1_out7);
  Clock clock (.out(clock_out));
  Register register_1 (.D(multiplexer_1_out), .en(and_1_out), .Q(register_1_q), .clk(clock_out));  // open: clr
  Register register_2 (.D(multiplexer_1_out), .en(and_2_out), .Q(register_2_q), .clk(clock_out));  // open: clr
  Register register_3 (.D(multiplexer_1_out), .en(and_3_out), .Q(register_3_q), .clk(clock_out));  // open: clr
  Register register_4 (.D(multiplexer_1_out), .en(and_4_out), .Q(register_4_q), .clk(clock_out));  // open: clr
  Register register_5 (.D(multiplexer_1_out), .en(and_5_out), .Q(register_5_q), .clk(clock_out));  // open: clr
  Register register_6 (.D(multiplexer_1_out), .en(and_6_out), .Q(register_6_q), .clk(clock_out));  // open: clr
  Register register_7 (.D(multiplexer_1_out), .en(and_7_out), .Q(register_7_q), .clk(clock_out));  // open: clr
  Register register_8 (.D(multiplexer_1_out), .en(and_8_out), .Q(register_8_q), .clk(clock_out));  // open: clr
  Multiplexer #(.select(3), .width(8), .enable("false")) multiplexer_2 (
    .in0(register_1_q), .in1(register_2_q), .in2(register_3_q), .in3(register_4_q), .in4(register_5_q),
    .in5(register_6_q), .in6(register_7_q), .in7(register_8_q), .out(out_7), .sel(in_2));
  Multiplexer #(.select(3), .width(8), .enable("false")) multiplexer_3 (
    .in0(register_1_q), .in1(register_2_q), .in2(register_3_q), .in3(register_4_q), .in4(register_5_q),
    .in5(register_6_q), .in6(register_7_q), .in7(register_8_q), .out(out_8), .sel(in_4));
endmodule
