// Logisim project ripple counter.circ as structural Verilog: 1 circuit, main circuit main
module main (
  input  in_1,
  output out_2,
  output out_3,
  output out_4,
  output out_5
);

  wire CLK_out, d_ff_1_qn, d_ff_2_qn, d_ff_3_qn, d_ff_4_qn, not_1_out, not_2_out, not_3_out, not_4_out,
       not_5_out, not_6_out, not_7_out, not_8_out;

  Clock CLK (.out(CLK_out));
  not not_1 (not_1_out, CLK_out);
  not not_2 (not_2_out, in_1);
  not not_3 (not_3_out, out_2);
  not not_4 (not_4_out, in_1);
  not not_5 (not_5_out, out_3);
  not not_6 (not_6_out, in_1);
  not not_7 (not_7_out, out_4);
  not not_8 (not_8_out, in_1);
  D_Flip_Flop d_ff_1 (
    .clk(not_1_out), .D(d_ff_1_qn), .Q(out_2), .Qn(d_ff_1_qn), .reset(not_2_out));  // open: preset, en
  D_Flip_Flop d_ff_2 (
    .clk(not_3_out), .D(d_ff_2_qn), .Q(out_3), .Qn(d_ff_2_qn), .reset(not_4_out));  // open: preset, en
  D_Flip_Flop d_ff_3 (
    .clk(not_5_out), .D(d_ff_3_qn), .Q(out_4), .Qn(d_ff_3_qn), .reset(not_6_out));  // open: preset, en
  D_Flip_Flop d_ff_4 (
    .clk(not_7_out), .D(d_ff_4_qn), .Q(out_5), .Qn(d_ff_4_qn), .reset(not_8_out));  // open: preset, en
endmodule
